// Logisim project 4bit_alu.circ as structural Verilog: 8 circuits, main circuit main
module main (
  input  A3,
  input  A2,
  input  A1,
  input  A0,
  input  B3,
  input  B2,
  input  B1,
  input  B0,
  input  [1:0] in_9,
  output P0,
  output P1,
  output P2,
  output P3,
  output overflow
);

  wire and_1_out, n4_bit_comparator_1_a_b, n4_bit_comparator_1_a_b_2, n4_bit_comparator_1_b_a,
       n4_bit_substractor_1_out_14, n4_bit_substractor_1_p0, n4_bit_substractor_1_p1,
       n4_bit_substractor_1_p2, n4_bit_substractor_1_p3, n4bit_adder_1_cout, n4bit_adder_1_out_10,
       n4bit_adder_1_out_11, n4bit_adder_1_out_12, n4bit_adder_1_out_13, or_1_out, xor_1_out;

  _4_bit_comparator u_4_bit_comparator_1 (
    .A3(A3), .A2(A2), .A1(A1), .A0(A0), .B3(B3), .B2(B2), .B1(B1), .B0(B0), .A_B(n4_bit_comparator_1_a_b),
    .A_B_2(n4_bit_comparator_1_a_b_2), .B_A(n4_bit_comparator_1_b_a));
  and and_1 (and_1_out, B3, B0, B1, B2, A3, A2, A1, A0);
  or or_1 (or_1_out, B3, B0, B1, B2, A3, A2, A1, A0);
  ExactlyOne xor_1 (.out(xor_1_out), .in0(A3), .in1(A2), .in2(A1), .in3(A0), .in4(B3), .in5(B2), .in6(B1), .in7(B0));
  _4bit_adder u_4bit_adder_1 (
    .in_9(1'b0), .A3(A3), .A2(A2), .A1(A1), .A0(A0), .B3(B3), .B2(B2), .B1(B1), .B0(B0),
    .Cout(n4bit_adder_1_cout), .out_10(n4bit_adder_1_out_10), .out_11(n4bit_adder_1_out_11),
    .out_12(n4bit_adder_1_out_12), .out_13(n4bit_adder_1_out_13));
  _4_bit_substractor u_4_bit_substractor_1 (
    .in_9(1'b0), .A3(A3), .A2(A2), .A1(A1), .A0(A0), .B3(B3), .B2(B2), .B1(B1), .B0(B0),
    .out_14(n4_bit_substractor_1_out_14), .P0(n4_bit_substractor_1_p0), .P1(n4_bit_substractor_1_p1),
    .P2(n4_bit_substractor_1_p2), .P3(n4_bit_substractor_1_p3));
  Multiplexer #(.select(2)) multiplexer_1 (
    .in0(n4bit_adder_1_out_10), .in1(n4_bit_substractor_1_p0), .in2(n4_bit_comparator_1_a_b),
    .in3(and_1_out), .out(P0), .sel(in_9));  // open: en
  Multiplexer #(.select(2)) multiplexer_2 (
    .in0(n4bit_adder_1_out_11), .in1(n4_bit_substractor_1_p1), .in2(n4_bit_comparator_1_a_b_2),
    .in3(or_1_out), .out(P1), .sel(in_9));  // open: en
  Multiplexer #(.select(2)) multiplexer_3 (
    .in0(n4bit_adder_1_out_12), .in1(n4_bit_substractor_1_p2), .in2(n4_bit_comparator_1_b_a),
    .in3(xor_1_out), .out(P2), .sel(in_9));  // open: en
  Multiplexer #(.select(2)) multiplexer_4 (
    .in0(n4bit_adder_1_out_13), .in1(n4_bit_substractor_1_p3), .in2(1'b0), .in3(1'b0), .out(P3), .sel(in_9));  // open: en
  Multiplexer #(.select(2)) multiplexer_5 (
    .in0(n4bit_adder_1_cout), .in1(n4_bit_substractor_1_out_14), .in2(1'b0), .in3(1'b0), .out(overflow),
    .sel(in_9));  // open: en

  // Notes on the sheet:
  //   00: add
  //   01:sub
  //   10:comp
  //   11: and
  //   AND
  //   A>B
  //   XOR
  //   OR
  //   A<B
  //   A=B
endmodule

module _2_bit_comparator (
  input  A1,
  input  A0,
  input  B1,
  input  B0,
  output A_B,
  output A_B_2,
  output A_B_3
);

  wire and_1_out, and_2_out, and_3_out, and_4_out, and_5_out, and_6_out, not_1_out, not_2_out, not_3_out,
       not_4_out, xnor_1_out, xnor_2_out;

  not not_1 (not_1_out, A1);
  not not_2 (not_2_out, B1);
  not not_3 (not_3_out, A0);
  not not_4 (not_4_out, B0);
  and and_1 (and_1_out, A1, not_2_out);
  and and_2 (and_2_out, not_2_out, not_4_out, A0);
  and and_3 (and_3_out, A1, A0, not_4_out);
  xnor xnor_1 (xnor_1_out, A0, B0);
  xnor xnor_2 (xnor_2_out, B1, A1);
  and and_4 (and_4_out, B1, not_1_out);
  and and_5 (and_5_out, not_3_out, B0, B1);
  and and_6 (and_6_out, not_3_out, not_1_out, B0);
  or or_1 (A_B, and_1_out, and_2_out, and_3_out);
  or or_2 (A_B_3, and_4_out, and_5_out, and_6_out);
  and and_7 (A_B_2, xnor_1_out, xnor_2_out);
endmodule

// compare
module _4_bit_comparator (
  input  A3,
  input  A2,
  input  A1,
  input  A0,
  input  B3,
  input  B2,
  input  B1,
  input  B0,
  output A_B,
  output A_B_2,
  output B_A
);

  wire and_1_out, and_2_out, n2_bit_comparator_1_a_b, n2_bit_comparator_1_a_b_2, n2_bit_comparator_1_a_b_3,
       n2_bit_comparator_2_a_b, n2_bit_comparator_2_a_b_2, n2_bit_comparator_2_a_b_3;

  _2_bit_comparator u_2_bit_comparator_1 (
    .A1(A1), .A0(A0), .B1(B1), .B0(B0), .A_B(n2_bit_comparator_1_a_b), .A_B_2(n2_bit_comparator_1_a_b_2),
    .A_B_3(n2_bit_comparator_1_a_b_3));
  _2_bit_comparator u_2_bit_comparator_2 (
    .A1(A3), .A0(A2), .B1(B3), .B0(B2), .A_B(n2_bit_comparator_2_a_b), .A_B_2(n2_bit_comparator_2_a_b_2),
    .A_B_3(n2_bit_comparator_2_a_b_3));
  and and_1 (and_1_out, n2_bit_comparator_2_a_b_2, n2_bit_comparator_1_a_b);
  and and_2 (and_2_out, n2_bit_comparator_2_a_b_2, n2_bit_comparator_1_a_b_3);
  and and_3 (A_B_2, n2_bit_comparator_2_a_b_2, n2_bit_comparator_1_a_b_2);
  or or_1 (B_A, n2_bit_comparator_2_a_b_3, and_2_out);
  or or_2 (A_B, n2_bit_comparator_2_a_b, and_1_out);
endmodule

module full_adder (
  input  A,
  input  B,
  input  Cin,
  output S,
  output Cout
);

  wire and_1_out, and_2_out, xor_1_out;

  xor xor_1 (xor_1_out, B, A);
  xor xor_2 (S, xor_1_out, Cin);
  and and_1 (and_1_out, xor_1_out, Cin);
  and and_2 (and_2_out, B, A);
  or or_1 (Cout, and_1_out, and_2_out);
endmodule

// add
module _4bit_adder (
  input  A3,
  input  A2,
  input  A1,
  input  A0,
  input  B3,
  input  B2,
  input  B1,
  input  B0,
  input  in_9,
  output out_10,
  output out_11,
  output out_12,
  output out_13,
  output Cout
);

  wire full_adder_1_cout, full_adder_2_cout, full_adder_3_cout;

  full_adder full_adder_1 (.Cin(in_9), .S(out_13), .Cout(full_adder_1_cout), .A(A0), .B(B0));
  full_adder full_adder_2 (.Cin(full_adder_1_cout), .S(out_12), .Cout(full_adder_2_cout), .A(A1), .B(B1));
  full_adder full_adder_3 (.Cin(full_adder_2_cout), .S(out_11), .Cout(full_adder_3_cout), .A(A2), .B(B2));
  full_adder full_adder_4 (.Cin(full_adder_3_cout), .S(out_10), .Cout(Cout), .A(A3), .B(B3));
endmodule

module full_substractor (
  input  A,
  input  B,
  input  Bin,
  output S,
  output Bout
);

  wire and_1_out, and_2_out, not_1_out, not_2_out, xor_1_out;

  not not_1 (not_1_out, A);
  xor xor_1 (xor_1_out, A, B);
  not not_2 (not_2_out, xor_1_out);
  and and_1 (and_1_out, Bin, not_2_out);
  and and_2 (and_2_out, not_1_out, B);
  xor xor_2 (S, xor_1_out, Bin);
  or or_1 (Bout, and_1_out, and_2_out);
endmodule

// sub
module _4_bit_substractor (
  input  A3,
  input  A2,
  input  A1,
  input  A0,
  input  B3,
  input  B2,
  input  B1,
  input  B0,
  input  in_9,
  output P0,
  output P1,
  output P2,
  output P3,
  output out_14
);

  wire full_substractor_1_bout, full_substractor_2_bout, full_substractor_3_bout;

  full_substractor full_substractor_1 (.Bin(in_9), .A(A0), .B(B0), .S(P0), .Bout(full_substractor_1_bout));
  full_substractor full_substractor_2 (
    .Bin(full_substractor_1_bout), .A(A1), .B(B1), .S(P1), .Bout(full_substractor_2_bout));
  full_substractor full_substractor_3 (
    .Bin(full_substractor_2_bout), .A(A2), .B(B2), .S(P2), .Bout(full_substractor_3_bout));
  full_substractor full_substractor_4 (.Bin(full_substractor_3_bout), .A(A3), .B(B3), .S(P3), .Bout(out_14));
endmodule

// 4bit ALU
module _4_bit_alu (
  input  A3,
  input  A2,
  input  A1,
  input  A0,
  input  B3,
  input  B2,
  input  B1,
  input  B0,
  input  [1:0] in_9,
  output P0,
  output P1,
  output P2,
  output P3,
  output overflow
);

  wire and_1_out, n4_bit_comparator_1_a_b, n4_bit_comparator_1_a_b_2, n4_bit_comparator_1_b_a,
       n4_bit_substractor_1_p0, n4_bit_substractor_1_p1, n4_bit_substractor_1_p2, n4_bit_substractor_1_p3,
       n4bit_adder_1_out_10, n4bit_adder_1_out_11, n4bit_adder_1_out_12, n4bit_adder_1_out_13, or_1_out,
       xor_1_out;

  _4_bit_comparator u_4_bit_comparator_1 (
    .A3(A3), .A2(A2), .A1(A1), .A0(A0), .B3(B3), .B2(B2), .B1(B1), .B0(B0), .A_B(n4_bit_comparator_1_a_b),
    .A_B_2(n4_bit_comparator_1_a_b_2), .B_A(n4_bit_comparator_1_b_a));
  and and_1 (and_1_out, B3, B0, B1, B2, A3, A2, A1, A0);
  or or_1 (or_1_out, B3, B0, B1, B2, A3, A2, A1, A0);
  ExactlyOne xor_1 (.out(xor_1_out), .in0(A3), .in1(A2), .in2(A1), .in3(A0), .in4(B3), .in5(B2), .in6(B1), .in7(B0));
  _4bit_adder u_4bit_adder_1 (
    .in_9(1'b0), .A3(A3), .A2(A2), .A1(A1), .A0(A0), .B3(B3), .B2(B2), .B1(B1), .B0(B0), .Cout(overflow),
    .out_10(n4bit_adder_1_out_10), .out_11(n4bit_adder_1_out_11), .out_12(n4bit_adder_1_out_12),
    .out_13(n4bit_adder_1_out_13));
  _4_bit_substractor u_4_bit_substractor_1 (
    .in_9(1'b0), .A3(A3), .A2(A2), .A1(A1), .A0(A0), .B3(B3), .B2(B2), .B1(B1), .B0(B0),
    .P0(n4_bit_substractor_1_p0), .P1(n4_bit_substractor_1_p1), .P2(n4_bit_substractor_1_p2),
    .P3(n4_bit_substractor_1_p3));  // open: out_14
  Multiplexer #(.select(2)) multiplexer_1 (
    .in0(n4bit_adder_1_out_10), .in1(n4_bit_substractor_1_p0), .in2(n4_bit_comparator_1_a_b),
    .in3(and_1_out), .out(P0), .sel(in_9));  // open: en
  Multiplexer #(.select(2)) multiplexer_2 (
    .in0(n4bit_adder_1_out_11), .in1(n4_bit_substractor_1_p1), .in2(n4_bit_comparator_1_a_b_2),
    .in3(or_1_out), .out(P1), .sel(in_9));  // open: en
  Multiplexer #(.select(2)) multiplexer_3 (
    .in0(n4bit_adder_1_out_12), .in1(n4_bit_substractor_1_p2), .in2(n4_bit_comparator_1_b_a),
    .in3(xor_1_out), .out(P2), .sel(in_9));  // open: en
  Multiplexer #(.select(2)) multiplexer_4 (
    .in0(n4bit_adder_1_out_13), .in1(n4_bit_substractor_1_p3), .in2(1'b0), .in3(1'b0), .out(P3), .sel(in_9));  // open: en

  // Notes on the sheet:
  //   00: add
  //   01:sub
  //   10:comp
  //   11: and
  //   AND
  //   A>B
  //   XOR
  //   OR
  //   A<B
  //   A=B
endmodule
